# Fritzing sketch NMCI_Fritzing_Sketch (saved by Fritzing 1.0.5)

parts:
  Mod1 = ESP32-TTGO-T-DISPLAY
  Bauteil1 = PN532 Elechouse RFID NFC Module V3

nets:
  N1: Mod1.3V, Bauteil1.VCC
  N2: Mod1.G-14, Bauteil1.GND
  N3: Mod1.26, Bauteil1.SDA
  N4: Mod1.25, Bauteil1.SCL

custom parts:
  ESP32-TTGO-T-DISPLAY: LILYGO TTGO T-Display GD32VF103CBT6 Main Chip ST7789 1.14 Inch IPS 240x135 Resolution Minimalist Development Board.
  PN532 Elechouse RFID NFC Module V3: NFC is a popular technology in recent years. We often heard this work while smart phone company such as Samsung or HTC introduces their latest high-end phones. Almost all the high-end phone in the market support NFC. Near field communication (NFC) is a set of standards for smart phones and similar devices to establish radio communication with each other by touching them together or bringing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
